// Logisim project 4bitAdder.circ as structural Verilog: 6 circuits, main circuit main
// Number Correct
module main (
  input  Enable_Halt
);

  wire and_2_out, CLK, Correct, Halt, not_1_out, not_2_out, NotDone, YourCout;
  wire [3:0] A, B, YourSum;
  wire [4:0] Solution;
  wire [8:0] Number_Correct_q;

  not not_1 (not_1_out, Correct);
  and and_1 (Halt, Enable_Halt, not_1_out);
  Clock clock_1 (.out(CLK));
  Inputs inputs_1 (.Halt(Halt), .Clk(CLK), .A(A), .B(B), .NotDone(NotDone));
  // Probe on A
  // Probe on B
  // Probe on YourSum
  // Probe on YourCout
  // Probe on Solution[3:0]
  // Probe on Solution[4]
  _4bitAdder _4BitAdder (.A(A), .B(B), .Cin(1'b0), .Sum(YourSum), .Cout(YourCout));
  not not_2 (not_2_out, Halt);
  and and_2 (and_2_out, Correct, NotDone, not_2_out);
  Checker checker_1 (.A(A), .B(B), .Sum(YourSum), .Cout(YourCout), .Correct(Correct), .CorrectAnswer(Solution));
  Counter #(.width(9), .max('h100)) Number_Correct (
    .count(and_2_out), .Q(Number_Correct_q), .clk(CLK));  // open: load, D, carry, clr
  // Probe on Number_Correct_q

  // Notes on the sheet:
  //   Use the Poke Tool on the enable halt input to enable/disable halting
  //   Enabling Halt will cause the testing to stop as soon as the first incorrect answer is detected
endmodule

module _4bitAdder (
  input  [3:0] A,
  input  [3:0] B,
  input  Cin,
  output [3:0] Sum,
  output Cout
);

  wire cla_1_c0, cla_1_c1, cla_1_c2, g0, G1, G2, G3, p0, P1, P2, P3;

  Full_Adder full_adder_1 (.A(A[0]), .B(B[0]), .Cin(Cin), .Sum(Sum[0]), .P(p0), .G(g0));
  Full_Adder full_adder_2 (.A(A[1]), .B(B[1]), .Cin(cla_1_c0), .Sum(Sum[1]), .P(P1), .G(G1));
  Full_Adder full_adder_3 (.A(A[2]), .B(B[2]), .Cin(cla_1_c1), .Sum(Sum[2]), .P(P2), .G(G2));
  CLA cla_1 (
    .g0(g0), .G1(G1), .G2(G2), .p0(p0), .P1(P1), .cin(Cin), .P2(P2), .Cin_2(Cin), .Cin_3(Cin), .P3(P3),
    .G3(G3), .Cin_4(Cin), .c0(cla_1_c0), .C1(cla_1_c1), .C2(cla_1_c2), .C3(Cout));
  Full_Adder full_adder_4 (.A(A[3]), .B(B[3]), .Cin(cla_1_c2), .Sum(Sum[3]), .P(P3), .G(G3));

  // Notes on the sheet:
  //   Full Adder 1
  //   s0
  //   s1
  //   Full Adder 2
  //   Full Adder 3
  //   cin
  //   s2
  //   CLA
  //   Full Adder 4
  //   s3
endmodule

module Inputs (
  input  Halt,
  input  Clk,
  output [3:0] A,
  output [3:0] B,
  output NotDone
);

  wire A_carry, and_1_out, and_2_out, and_3_out, and_4_out, CarryB, Delay_q, nHalt;

  not not_1 (nHalt, Halt);
  and and_1 (and_1_out, nHalt, NotDone);
  Counter #(.width(4), .max('hf)) u_B (.count(and_1_out), .Q(B), .carry(CarryB), .clk(Clk));  // open: load, D, clr
  and and_2 (and_2_out, nHalt, CarryB);
  Counter #(.width(4), .max('hf), .ongoal("stay")) u_A (
    .count(and_2_out), .Q(A), .carry(A_carry), .clk(Clk));  // open: load, D, clr
  and and_3 (and_3_out, CarryB, A_carry);
  Register #(.width(1)) Delay (.D(and_3_out), .en(and_4_out), .Q(Delay_q), .clk(Clk));  // open: clr
  and and_4 (and_4_out, nHalt, NotDone);
  not not_2 (NotDone, Delay_q);
endmodule

module Checker (
  input  [3:0] A,
  input  [3:0] B,
  input  [3:0] Sum,
  input  Cout,
  output Correct,
  output [4:0] CorrectAnswer
);

  ROM #(.dataWidth(5)) rom_1 (.addr({A, B}), .data(CorrectAnswer));  // open: sel
  Comparator #(.width(5), .mode("unsigned")) comparator_1 (
    .a(CorrectAnswer), .b({Cout, Sum}), .eq(Correct));  // open: gt, lt

  // Other names for the same wires on the sheet: StudentSol[4:0] = {Cout, Sum}

  // Notes on the sheet:
  //   contents of rom_1 (hex, n*v repeats v):
  //   0 1 2 3 4 5 6 7 8 9 a b c d e f 1 2 3 4 5 6 7 8 9 a b c d e f 10 2 3 4 5 6 7 8 9 a b c d e f 10 11 3
  //   4 5 6 7 8 9 a b c d e f 10 11 12 4 5 6 7 8 9 a b c d e f 10 11 12 13 5 6 7 8 9 a b c d e f 10 11 12
  //   13 14 6 7 8 9 a b c d e f 10 11 12 13 14 15 7 8 9 a b c d e f 10 11 12 13 14 15 16 8 9 a b c d e f
  //   10 11 12 13 14 15 16 17 9 a b c d e f 10 11 12 13 14 15 16 17 18 a b c d e f 10 11 12 13 14 15 16 17
  //   18 19 b c d e f 10 11 12 13 14 15 16 17 18 19 1a c d e f 10 11 12 13 14 15 16 17 18 19 1a 1b d e f
  //   10 11 12 13 14 15 16 17 18 19 1a 1b 1c e f 10 11 12 13 14 15 16 17 18 19 1a 1b 1c 1d f 10 11 12 13
  //   14 15 16 17 18 19 1a 1b 1c 1d 1e
endmodule

module Full_Adder (
  input  A,
  input  B,
  input  Cin,
  output Sum,
  output P,
  output G
);

  xor odd_parity_1 (Sum, A, B, Cin);
  or or_1 (P, A, B);
  and and_1 (G, A, B);
endmodule

module CLA (
  input  g0,
  input  G1,
  input  G2,
  input  p0,
  input  P1,
  input  cin,
  input  P2,
  input  Cin_2,
  input  Cin_3,
  input  P3,
  input  G3,
  input  Cin_4,
  output c0,
  output C1,
  output C2,
  output C3
);

  wire and_1_out, and_2_out, and_3_out, and_4_out, and_5_out, and_6_out, and_7_out, and_8_out, and_9_out,
       and_10_out;

  and and_1 (and_1_out, p0, cin);
  or or_1 (c0, g0, and_1_out);
  and and_2 (and_2_out, P1, g0);
  and and_3 (and_3_out, P1, p0, Cin_2);
  or or_2 (C1, G1, and_2_out, and_3_out);
  and and_4 (and_4_out, P2, G1);
  and and_5 (and_5_out, P2, P1, g0);
  and and_6 (and_6_out, P2, P1, p0, Cin_3);
  or or_3 (C2, G2, and_4_out, and_5_out, and_6_out);
  and and_7 (and_7_out, P3, G2);
  and and_8 (and_8_out, P3, P2, G1);
  and and_9 (and_9_out, P3, P1, g0, P2);
  and and_10 (and_10_out, P3, P2, P1, p0, Cin_4);
  or or_4 (C3, G3, and_7_out, and_8_out, and_9_out, and_10_out);
endmodule
