// Logisim project 4bitAdderSub.circ as structural Verilog: 8 circuits, main circuit main
module main (
  input  g0,
  input  p0,
  input  cin,
  output c0
);

  wire and_1_out;

  and and_1 (and_1_out, p0, cin);
  or or_1 (c0, g0, and_1_out);
endmodule

module c1 (
  input  G1,
  input  P1,
  input  G0,
  input  P0,
  input  Cin,
  output C1
);

  wire and_1_out, and_2_out;

  and and_1 (and_1_out, P1, G0);
  and and_2 (and_2_out, P1, P0, Cin);
  or or_1 (C1, G1, and_1_out, and_2_out);
endmodule

module c2 (
  input  G2,
  input  G1,
  input  P2,
  input  P1,
  input  P0,
  input  Cin,
  input  G0,
  output C2
);

  wire and_1_out, and_2_out, and_3_out;

  and and_1 (and_1_out, P2, G1);
  and and_2 (and_2_out, P2, P1, G0);
  and and_3 (and_3_out, P2, P1, P0, Cin);
  or or_1 (C2, G2, and_1_out, and_2_out, and_3_out);
endmodule

module c3 (
  input  P0,
  input  G0,
  input  G1,
  input  P1,
  input  P2,
  input  G2,
  input  P3,
  input  G3,
  input  Cin,
  output C3
);

  wire and_1_out, and_2_out, and_3_out, and_4_out;

  and and_1 (and_1_out, P3, G2);
  and and_2 (and_2_out, P3, P2, G1);
  and and_3 (and_3_out, P3, P1, G0, P2);
  and and_4 (and_4_out, P3, P2, P1, P0, Cin);
  or or_1 (C3, G3, and_1_out, and_2_out, and_3_out, and_4_out);
endmodule

module Full_Adder (
  input  A,
  input  B,
  input  Cin,
  output Sum,
  output P,
  output G
);

  xor odd_parity_1 (Sum, A, B, Cin);
  or or_1 (P, A, B);
  and and_1 (G, A, B);
endmodule

module FULL_CLA (
  input  g0,
  input  G1,
  input  G2,
  input  p0,
  input  P1,
  input  G1_2,
  input  cin,
  input  G0_2,
  input  P2,
  input  P0_2,
  input  P0_3,
  input  P1_2,
  input  G0_3,
  input  P0_4,
  input  G1_3,
  input  P1_3,
  input  G0_4,
  input  P2_2,
  input  G2_2,
  input  P3,
  input  G3,
  output C3
);

  wire and_1_out, and_2_out, and_3_out, and_4_out, and_5_out, and_6_out, and_7_out, and_8_out, and_9_out,
       and_10_out, or_1_out, or_2_out, or_3_out;

  and and_1 (and_1_out, p0, cin);
  or or_1 (or_1_out, g0, and_1_out);
  and and_2 (and_2_out, P1, G0_2);
  and and_3 (and_3_out, P1, P0_3, or_1_out);
  or or_2 (or_2_out, G1, and_2_out, and_3_out);
  and and_4 (and_4_out, P2, G1_2);
  and and_5 (and_5_out, P2, P1_2, G0_4);
  and and_6 (and_6_out, P2, P1_2, P0_4, or_2_out);
  or or_3 (or_3_out, G2, and_4_out, and_5_out, and_6_out);
  and and_7 (and_7_out, P3, G2_2);
  and and_8 (and_8_out, P3, P2_2, G1_3);
  and and_9 (and_9_out, P3, P1_3, G0_3, P2_2);
  and and_10 (and_10_out, P3, P2_2, P1_3, P0_2, or_3_out);
  or or_4 (C3, G3, and_7_out, and_8_out, and_9_out, and_10_out);
endmodule

module FULL_CON (
  input  g0,
  input  G1,
  input  G2,
  input  p0,
  input  P1,
  input  cin,
  input  P2,
  input  P3,
  input  G3,
  output C3
);

  wire and_1_out, and_2_out, and_3_out, and_4_out, and_5_out, and_6_out, and_7_out, and_8_out, and_9_out,
       and_10_out, or_1_out, or_2_out, or_3_out;

  and and_1 (and_1_out, p0, cin);
  or or_1 (or_1_out, g0, and_1_out);
  and and_2 (and_2_out, P1, g0);
  and and_3 (and_3_out, P1, p0, or_1_out);
  or or_2 (or_2_out, G1, and_2_out, and_3_out);
  and and_4 (and_4_out, P2, G1);
  and and_5 (and_5_out, P2, P1, g0);
  and and_6 (and_6_out, P2, P1, p0, or_2_out);
  or or_3 (or_3_out, G2, and_4_out, and_5_out, and_6_out);
  and and_7 (and_7_out, P3, G2);
  and and_8 (and_8_out, P3, P2, G1);
  and and_9 (and_9_out, P3, P1, g0, P2);
  and and_10 (and_10_out, P3, P2, P1, p0, or_3_out);
  or or_4 (C3, G3, and_7_out, and_8_out, and_9_out, and_10_out);
endmodule

module _4bit (
);

  wire full_con_1_c3, g0, G1, G2, G3, p0, P1, P2, P3, undriven;

  FULL_CON full_con_1 (
    .g0(g0), .G1(G1), .G2(G2), .p0(p0), .P1(P1), .cin(undriven), .P2(P2), .P3(P3), .G3(G3), .C3(full_con_1_c3));

  // Notes on the sheet:
  //   cin
  //   CLA
endmodule
