// Logisim project UpDownCounter-2.circ as structural Verilog: 5 circuits, main circuit main
module main (
  input  Halt_Enable
);

  wire and_2_out, CLK, Correct, Count_Down, Count_Up, Done_Testing, Halt, not_1_out, not_2_out, not_3_out;
  wire [2:0] Solution, Your_Answer;
  wire [5:0] counter_1_q;

  not not_1 (not_1_out, Correct);
  Clock clock_1 (.out(CLK));
  and and_1 (Halt, Halt_Enable, not_1_out);
  Inputs inputs_1 (.Halt(Halt), .CLK(CLK), .Count_Up(Count_Up), .Count_Down(Count_Down), .Done_Testing(Done_Testing));
  // Probe on Count_Up
  // Probe on Count_Down
  // Probe on Your_Answer
  // Probe on Solution
  Up_Down_Counter up_down_counter_1 (.Count_Up(Count_Up), .Count_Down(Count_Down), .CLK(CLK), .Count(Your_Answer));
  not not_2 (not_2_out, Halt);
  not not_3 (not_3_out, Done_Testing);
  Counter #(.width(6), .max('h21), .ongoal("stay")) counter_1 (
    .count(and_2_out), .Q(counter_1_q), .clk(CLK));  // open: load, D, carry, clr
  and and_2 (and_2_out, Correct, not_2_out, not_3_out);
  Checker checker_1 (
    .Halt_Enable(Halt_Enable), .Count_Up(Count_Up), .Count_Donw(Count_Down), .Your_Answer(Your_Answer),
    .CLK(CLK), .Correct(Correct), .Solution(Solution));
  // Probe on counter_1_q

  // Notes on the sheet:
  //   Your Solution in Here
  //   Max of 33
endmodule

module Up_Down_Counter (
  input  Count_Up,
  input  Count_Down,
  input  CLK,
  output [2:0] Count
);

  wire [2:0] sub_1_s0p;

  sub sub_1 (
    .S2(Count[2]), .S1(Count[1]), .S0(Count[0]), .UP(Count_Up), .DOWN(Count_Down), .S2P(sub_1_s0p[2]),
    .S1P(sub_1_s0p[1]), .S0P(sub_1_s0p[0]));
  Register #(.width(3)) u_Count (.D(sub_1_s0p), .Q(Count), .clk(CLK));  // open: en, clr
endmodule

module Inputs (
  input  Halt,
  input  CLK,
  output Count_Up,
  output Count_Down,
  output Done_Testing
);

  wire not_1_out;
  wire [5:0] counter_1_q;

  not not_1 (not_1_out, Halt);
  Counter #(.width(6), .max('h21), .ongoal("stay")) counter_1 (
    .count(not_1_out), .Q(counter_1_q), .carry(Done_Testing), .clk(CLK));  // open: load, D, clr
  ROM #(.addrWidth(6), .dataWidth(2)) rom_1 (.addr(counter_1_q), .data({Count_Up, Count_Down}));  // open: sel

  // Notes on the sheet:
  //   contents of rom_1 (hex, n*v repeats v):
  //   0 2 0 2 0 2 0 2 0 2 0 2 0 2 0 2 0 1 0 1 0 1 0 1 0 1 0 1 0 1 0 1
endmodule

module Checker (
  input  Halt_Enable,
  input  Count_Up,
  input  Count_Donw,
  input  [2:0] Your_Answer,
  input  CLK,
  output Correct,
  output [2:0] Solution
);

  wire and_1_out, and_2_out, and_3_out, Gate, nHalt_Enable, or_2_out;

  not not_1 (nHalt_Enable, Halt_Enable);
  and and_1 (and_1_out, Correct, Halt_Enable);
  and and_2 (and_2_out, Count_Up, Gate);
  or or_1 (Gate, nHalt_Enable, and_1_out);
  and and_3 (and_3_out, Gate, Count_Donw);
  or or_2 (or_2_out, and_3_out, and_2_out);
  Counter #(.width(3), .max('h7), .ongoal("stay")) counter_1 (
    .load(and_3_out), .count(or_2_out), .Q(Solution), .clk(CLK));  // open: D, carry, clr
  Comparator #(.width(3)) comparator_1 (.a(Solution), .b(Your_Answer), .eq(Correct));  // open: gt, lt

  // Other names for the same wires on the sheet: Count_Down = Count_Donw
endmodule

module sub (
  input  S2,
  input  S1,
  input  S0,
  input  UP,
  input  DOWN,
  output S2P,
  output S1P,
  output S0P
);

  wire and_1_out, and_2_out, and_3_out, and_4_out, and_5_out, and_6_out, and_7_out, and_8_out, and_9_out,
       and_10_out, and_11_out, and_12_out, and_13_out, and_14_out, and_15_out, and_16_out, and_17_out,
       not_1_out, not_2_out, not_3_out, not_4_out, not_5_out, not_6_out, not_7_out, not_8_out, not_9_out,
       not_10_out, not_11_out, not_12_out, not_13_out, not_14_out, not_15_out, not_16_out, not_17_out,
       not_18_out;

  not not_1 (not_1_out, DOWN);
  not not_2 (not_2_out, DOWN);
  not not_3 (not_3_out, S1);
  not not_4 (not_4_out, DOWN);
  not not_5 (not_5_out, UP);
  not not_6 (not_6_out, DOWN);
  not not_7 (not_7_out, S0);
  not not_8 (not_8_out, S1);
  not not_9 (not_9_out, S0);
  not not_10 (not_10_out, UP);
  not not_11 (not_11_out, S0);
  not not_12 (not_12_out, DOWN);
  not not_13 (not_13_out, UP);
  not not_14 (not_14_out, DOWN);
  not not_15 (not_15_out, S0);
  not not_16 (not_16_out, UP);
  not not_17 (not_17_out, S0);
  not not_18 (not_18_out, UP);
  and and_1 (and_1_out, S1, S0, UP, not_1_out);
  and and_2 (and_2_out, S2, not_2_out);
  and and_3 (and_3_out, S2, UP);
  and and_4 (and_4_out, S2, S0);
  and and_5 (and_5_out, S2, S1);
  and and_6 (and_6_out, not_3_out, S0, UP, not_4_out);
  and and_7 (and_7_out, S1, not_5_out, not_6_out);
  and and_8 (and_8_out, S1, not_7_out, UP);
  and and_9 (and_9_out, S1, S0, DOWN);
  and and_10 (and_10_out, S2, not_8_out, not_9_out, not_10_out, DOWN);
  and and_11 (and_11_out, S2, S1, S0);
  and and_12 (and_12_out, not_11_out, UP, not_12_out);
  and and_13 (and_13_out, S0, not_13_out, not_14_out);
  and and_14 (and_14_out, S0, UP, DOWN);
  and and_15 (and_15_out, S1, not_15_out, not_16_out, DOWN);
  and and_16 (and_16_out, S2, not_17_out, not_18_out, DOWN);
  and and_17 (and_17_out, S2, S1, S0, UP);
  or or_1 (S2P, and_1_out, and_2_out, and_3_out, and_4_out, and_5_out);
  or or_2 (S1P, and_6_out, and_7_out, and_8_out, and_9_out, and_10_out, and_11_out);
  or or_3 (S0P, and_12_out, and_13_out, and_14_out, and_15_out, and_16_out, and_17_out);
endmodule
