// Logisim project Vending.circ as structural Verilog: 6 circuits, main circuit main
module main (
  input  Halt_Enable
);

  wire and_2_out, CLK, Correct, Dime, Done_Testing, Give_Dime, Give_Merch, Give_Nickel, Halt, Nickel,
       not_1_out, not_2_out, not_3_out, Quarter, Sol_Give_Dime, Sol_Give_Merch, Sol_Give_Nickel;
  wire [8:0] counter_1_q, TestNumber;

  Clock clock_1 (.out(CLK));
  not not_1 (not_1_out, Correct);
  and and_1 (Halt, Halt_Enable, not_1_out);
  Inputs inputs_1 (
    .Halt(Halt), .CLK(CLK), .Quarter(Quarter), .Dime(Dime), .Nickel(Nickel), .TestNumber(TestNumber),
    .Done_Testing(Done_Testing));
  // Probe on Quarter
  // Probe on Dime
  // Probe on Nickel
  Vending vending_1 (
    .Quarter(Quarter), .Dime(Dime), .Nickel(Nickel), .CLK(CLK), .Give_Merchandise(Give_Merch),
    .Give_Dime(Give_Dime), .Give_Nickel(Give_Nickel));
  // Probe on Correct
  // Probe on Give_Merch
  // Probe on Sol_Give_Merch
  // Probe on Give_Dime
  // Probe on Sol_Give_Dime
  // Probe on Give_Nickel
  // Probe on Sol_Give_Nickel
  not not_2 (not_2_out, Halt);
  Checker checker_1 (
    .Give_Merch(Give_Merch), .Give_Dime(Give_Dime), .Give_Nickel(Give_Nickel), .TestNumber(TestNumber),
    .Correct(Correct), .Sol_Give_Merch(Sol_Give_Merch), .Sol_Give_Dime(Sol_Give_Dime),
    .Sol_Give_Nickel(Sol_Give_Nickel));
  and and_2 (and_2_out, Correct, not_2_out, not_3_out);
  not not_3 (not_3_out, Done_Testing);
  // Probe on counter_1_q
  Counter #(.width(9), .max('h162), .ongoal("stay")) counter_1 (
    .count(and_2_out), .Q(counter_1_q), .clk(CLK));  // open: load, D, carry, clr

  // Notes on the sheet:
  //   Max 354
endmodule

module Vending (
  input  Quarter,
  input  Dime,
  input  Nickel,
  input  CLK,
  output Give_Merchandise,
  output Give_Dime,
  output Give_Nickel
);

  wire s0, s0P, s1, s1P, s2, s2P;

  NextState nextstate_1 (
    .s2(s2), .s1(s1), .s0(s0), .x3(Quarter), .x2(Dime), .x1(Nickel), .s2P(s2P), .s1P(s1P), .s0P(s0P));
  Register #(.width(3)) register_1 (.D({s2P, s1P, s0P}), .Q({s2, s1, s0}), .clk(CLK));  // open: en, clr
  Output output_1 (
    .s2(s2), .s1(s1), .s0(s0), .x3(Quarter), .x2(Dime), .x1(Nickel), .GM(Give_Merchandise), .GD(Give_Dime),
    .GN(Give_Nickel));

  // Other names for the same wires on the sheet: Quater = Quarter
endmodule

module Inputs (
  input  Halt,
  input  CLK,
  output Quarter,
  output Dime,
  output Nickel,
  output [8:0] TestNumber,
  output Done_Testing
);

  wire not_1_out;

  not not_1 (not_1_out, Halt);
  Counter #(.width(9), .max('h162), .ongoal("stay")) counter_1 (
    .count(not_1_out), .Q(TestNumber), .carry(Done_Testing), .clk(CLK));  // open: load, D, clr
  ROM #(.addrWidth(9), .dataWidth(3)) rom_1 (.addr(TestNumber), .data({Quarter, Dime, Nickel}));  // open: sel

  // Notes on the sheet:
  //   contents of rom_1 (hex, n*v repeats v):
  //   1 0 1 0 1 0 1 0 1 0 1 0 1 0 1 0 1 0 1 0 1 0 2 0 1 0 1 0 1 0 1 0 1 0 4 0 1 0 1 0 1 0 1 0 2 0 1 0 1 0
  //   1 0 1 0 4 0 1 0 1 0 1 0 1 0 2 0 1 0 1 0 1 0 2 0 2 0 1 0 1 0 1 0 2 0 4 0 1 0 1 0 1 0 4 0 1 0 1 0 1 0
  //   1 0 2 0 1 0 1 0 1 0 2 0 2 0 1 0 1 0 1 0 2 0 4 0 1 0 1 0 2 0 2 0 1 0 1 0 2 0 4 0 1 0 1 0 4 0 1 0 1 0
  //   1 0 1 0 2 0 1 0 1 0 1 0 2 0 2 0 1 0 1 0 1 0 2 0 4 0 1 0 1 0 2 0 2 0 1 0 1 0 2 0 4 0 1 0 1 0 2 0 2 0
  //   1 0 2 0 2 0 2 0 1 0 2 0 2 0 4 0 1 0 2 0 4 0 1 0 4 0 1 0 1 0 1 0 1 0 2 0 1 0 1 0 1 0 2 0 2 0 1 0 1 0
  //   1 0 2 0 4 0 1 0 1 0 2 0 2 0 1 0 1 0 2 0 4 0 1 0 1 0 2 0 2 0 1 0 2 0 2 0 2 0 1 0 2 0 2 0 4 0 1 0 2 0
  //   4 0 1 0 1 0 2 0 2 0 1 0 2 0 2 0 2 0 1 0 2 0 2 0 4 0 2 0 2 0 2 0 2 0 2 0 4 0 2 0 4 0 1 0 4 0 2 0 4 0
  //   4 0 4
endmodule

module Checker (
  input  Give_Merch,
  input  Give_Dime,
  input  Give_Nickel,
  input  [8:0] TestNumber,
  output Correct,
  output Sol_Give_Merch,
  output Sol_Give_Dime,
  output Sol_Give_Nickel
);

  ROM #(.addrWidth(9), .dataWidth(3)) rom_1 (
    .addr(TestNumber), .data({Sol_Give_Merch, Sol_Give_Dime, Sol_Give_Nickel}));  // open: sel
  Comparator #(.width(3)) comparator_1 (
    .a({Sol_Give_Merch, Sol_Give_Dime, Sol_Give_Nickel}), .b({Give_Merch, Give_Dime, Give_Nickel}),
    .eq(Correct));  // open: gt, lt

  // Other names for the same wires on the sheet: Solution[2:0] = {Sol_Give_Merch, Sol_Give_Dime, Sol_Give_Nickel};
  //   Your_Answer[2:0] = {Give_Merch, Give_Dime, Give_Nickel}

  // Notes on the sheet:
  //   contents of rom_1 (hex, n*v repeats v):
  //   10*0 4 11*0 5 11*0 7 9*0 4 9*0 7 9*0 4 9*0 5 9*0 7 7*0 6 9*0 4 9*0 5 9*0 7 7*0 4 7*0 7 5*0 5 9*0 4
  //   9*0 5 9*0 7 7*0 4 7*0 7 7*0 4 7*0 5 7*0 7 5*0 6 0 0 0 4 9*0 4 9*0 5 9*0 7 7*0 4 7*0 7 7*0 4 7*0 5
  //   7*0 7 5*0 6 7*0 4 7*0 5 7*0 7 5*0 4 5*0 7 0 0 0 5 0 0 0 4 0 0 0 5 0 0 0 7
endmodule

module NextState (
  input  s2,
  input  s1,
  input  s0,
  input  x3,
  input  x2,
  input  x1,
  output s2P,
  output s1P,
  output s0P
);

  wire and_1_out, and_2_out, and_3_out, and_4_out, and_5_out, and_6_out, and_7_out, and_8_out, and_9_out,
       and_10_out, and_11_out, and_12_out, and_13_out, and_14_out, and_15_out, and_16_out, and_17_out,
       and_18_out, and_19_out, and_20_out, and_21_out, and_22_out, not_1_out, not_2_out, not_3_out,
       not_4_out, not_5_out, not_6_out, not_7_out, not_8_out, not_9_out, not_10_out, not_11_out, not_12_out,
       not_13_out, not_14_out, not_15_out, not_16_out, not_17_out, not_18_out, not_19_out, not_20_out,
       not_21_out, not_22_out, not_23_out, not_24_out, not_25_out, not_26_out, not_27_out, not_28_out,
       not_29_out, not_30_out, not_31_out, not_32_out, not_33_out, not_34_out, not_35_out, not_36_out,
       not_37_out, not_38_out, not_39_out, not_40_out, not_41_out, not_42_out, not_43_out, not_44_out;

  not not_1 (not_1_out, s2);
  not not_2 (not_2_out, s0);
  not not_3 (not_3_out, x3);
  not not_4 (not_4_out, x1);
  not not_5 (not_5_out, s0);
  not not_6 (not_6_out, x3);
  not not_7 (not_7_out, x2);
  not not_8 (not_8_out, x3);
  not not_9 (not_9_out, x2);
  not not_10 (not_10_out, x1);
  not not_11 (not_11_out, s2);
  not not_12 (not_12_out, s1);
  not not_13 (not_13_out, x3);
  not not_14 (not_14_out, x2);
  not not_15 (not_15_out, s2);
  not not_16 (not_16_out, s0);
  not not_17 (not_17_out, x3);
  not not_18 (not_18_out, x2);
  not not_19 (not_19_out, s1);
  not not_20 (not_20_out, s0);
  not not_21 (not_21_out, x3);
  not not_22 (not_22_out, x1);
  not not_23 (not_23_out, s2);
  not not_24 (not_24_out, s1);
  not not_25 (not_25_out, s0);
  not not_26 (not_26_out, x2);
  not not_27 (not_27_out, x1);
  not not_28 (not_28_out, x3);
  not not_29 (not_29_out, x2);
  not not_30 (not_30_out, x1);
  not not_31 (not_31_out, s2);
  not not_32 (not_32_out, s1);
  not not_33 (not_33_out, s0);
  not not_34 (not_34_out, x2);
  not not_35 (not_35_out, x1);
  not not_36 (not_36_out, x3);
  not not_37 (not_37_out, x2);
  not not_38 (not_38_out, x1);
  not not_39 (not_39_out, s1);
  not not_40 (not_40_out, s1);
  not not_41 (not_41_out, x3);
  not not_42 (not_42_out, x2);
  not not_43 (not_43_out, x3);
  not not_44 (not_44_out, x1);
  and and_1 (and_1_out, not_1_out, not_2_out, not_3_out, x2, not_4_out);
  and and_2 (and_2_out, s1, not_5_out, not_6_out, not_7_out, x1);
  and and_3 (and_3_out, s2, not_8_out, not_9_out, not_10_out);
  and and_4 (and_4_out, s2, x2, x1);
  and and_5 (and_5_out, s2, x3, x1);
  and and_6 (and_6_out, s2, x3, x2);
  and and_7 (and_7_out, not_11_out, not_12_out, not_13_out, not_14_out, x1);
  and and_8 (and_8_out, not_15_out, not_16_out, not_17_out, not_18_out, x1);
  and and_9 (and_9_out, not_19_out, not_20_out, not_21_out, x2, not_22_out);
  and and_10 (and_10_out, not_23_out, not_24_out, not_25_out, x3, not_26_out, not_27_out);
  and and_11 (and_11_out, s1, not_28_out, not_29_out, not_30_out);
  and and_12 (and_12_out, s1, x2, x1);
  and and_13 (and_13_out, s1, x3, x1);
  and and_14 (and_14_out, s1, x3, x2);
  and and_15 (and_15_out, not_31_out, not_32_out, not_33_out, x3, not_34_out, not_35_out);
  and and_16 (and_16_out, s0, not_36_out, not_37_out, not_38_out);
  and and_17 (and_17_out, not_39_out, s0, x1);
  and and_18 (and_18_out, s0, x2, x1);
  and and_19 (and_19_out, s0, x3, x1);
  and and_20 (and_20_out, s0, x3, x2);
  and and_21 (and_21_out, s2, not_40_out, not_41_out, not_42_out, x1);
  and and_22 (and_22_out, s2, not_43_out, x2, not_44_out);
  or or_1 (s2P, and_1_out, and_2_out, and_3_out, and_4_out, and_5_out, and_6_out);
  or or_2 (s1P, and_7_out, and_8_out, and_9_out, and_10_out, and_11_out, and_12_out, and_13_out, and_14_out);
  or or_3 (s0P, and_15_out, and_16_out, and_17_out, and_18_out, and_19_out, and_20_out, and_21_out, and_22_out);
endmodule

module Output (
  input  s2,
  input  s1,
  input  s0,
  input  x3,
  input  x2,
  input  x1,
  output GM,
  output GD,
  output GN
);

  wire and_1_out, and_2_out, and_3_out, and_4_out, and_5_out, and_6_out, and_7_out, and_8_out, and_9_out,
       and_10_out, not_1_out, not_2_out, not_3_out, not_4_out, not_5_out, not_6_out, not_7_out, not_8_out,
       not_9_out, not_10_out, not_11_out, not_12_out, not_13_out, not_14_out, not_15_out, not_16_out,
       not_17_out, not_18_out, not_19_out, not_20_out, not_21_out;

  not not_1 (not_1_out, x3);
  not not_2 (not_2_out, x1);
  not not_3 (not_3_out, x2);
  not not_4 (not_4_out, x1);
  not not_5 (not_5_out, x2);
  not not_6 (not_6_out, x1);
  not not_7 (not_7_out, x3);
  not not_8 (not_8_out, x2);
  not not_9 (not_9_out, x2);
  not not_10 (not_10_out, x1);
  not not_11 (not_11_out, x2);
  not not_12 (not_12_out, x1);
  not not_13 (not_13_out, s1);
  not not_14 (not_14_out, x2);
  not not_15 (not_15_out, x1);
  not not_16 (not_16_out, x2);
  not not_17 (not_17_out, x1);
  not not_18 (not_18_out, x3);
  not not_19 (not_19_out, x1);
  not not_20 (not_20_out, x2);
  not not_21 (not_21_out, x1);
  and and_1 (and_1_out, s0, not_1_out, x2, not_2_out);
  and and_2 (and_2_out, s0, x3, not_3_out, not_4_out);
  and and_3 (and_3_out, s1, x3, not_5_out, not_6_out);
  and and_4 (and_4_out, s1, s0, not_7_out, not_8_out, x1);
  and and_5 (and_5_out, s2, x3, not_9_out, not_10_out);
  and and_6 (and_6_out, s0, x3, not_11_out, not_12_out);
  and and_7 (and_7_out, s2, not_13_out, x3, not_14_out, not_15_out);
  and and_8 (and_8_out, s0, x3, not_16_out, not_17_out);
  and and_9 (and_9_out, s1, s0, not_18_out, x2, not_19_out);
  and and_10 (and_10_out, s2, s1, x3, not_20_out, not_21_out);
  or or_1 (GM, and_1_out, and_2_out, and_3_out, and_4_out, and_5_out);
  or or_2 (GD, and_6_out, and_7_out);
  or or_3 (GN, and_8_out, and_9_out, and_10_out);
endmodule
