// Logisim project example.circ as structural Verilog: 2 circuits, main circuit main
module main (
  input  A,
  input  B,
  output out_3,
  output Y2,
  output [1:0] out_5
);

  wire clock;

  subcircuit subcircuit_1 (.A(A), .B(B), .\output (out_3));  // open: out_4
  Clock clock_1 (.out(clock));

  assign out_5 = {B, out_3};
  assign Y2 = out_3;

  // Other names for the same wires on the sheet: Y = out_3

  // Notes on the sheet:
  //   Subcircuit
  //   Splitter / Bus
endmodule

module subcircuit (
  input  A,
  input  B,
  output \output ,
  output out_4
);

  wire and_1_out, or_1_out;

  and and_1 (and_1_out, A, B);
  or or_1 (or_1_out, A, and_1_out);
  not not_1 (\output , or_1_out);

  // Other names for the same wires on the sheet: Y = out_4

  // Notes on the sheet:
  //   subcircuit
endmodule
